# Fritzing sketch OneWireTemperature (saved by Fritzing 0.9.0b)
breadboards: 1

parts:
  MVPROG1 = MicroView with Programmer [part_number=MicroView package="16pin wide"]
  DS18B20_TempSensor1 = DS18B20 TempSensor [part_number=DFR0024]

nets:
  GND: MVPROG1.GND, DS18B20_TempSensor1.GND
  N1: MVPROG1.D3, DS18B20_TempSensor1.INPUT
  N2: MVPROG1.5V, DS18B20_TempSensor1.POWER

custom parts:
  MicroView with Programmer: MicroView - Chip-sized Arduino with OLED display.
  DS18B20 TempSensor: OneWire DS18B20 Temperature Sensor
